// Logisim project 16x4_mux.circ as structural Verilog: 1 circuit, main circuit main
module main (
  input  S1,
  input  S0,
  input  A3,
  input  A2,
  input  A1,
  input  A0,
  input  B3,
  input  B2,
  input  B1,
  input  B0,
  input  C3,
  input  C2,
  input  C1,
  input  C0,
  input  D3,
  input  D2,
  input  D1,
  input  D0,
  output Out3,
  output Out2,
  output Out1,
  output Out0
);

  wire Bit_0_2_out, Bit_0_3_out, Bit_0_4_out, Bit_0_5_out, Bit_0_6_out, Bit_0_7_out, Bit_0_8_out, Bit_0_out,
       Bit_1_2_out, Bit_1_3_out, Bit_1_4_out, Bit_1_5_out, Bit_1_6_out, Bit_1_7_out, Bit_1_8_out, Bit_1_out,
       Bit_2_2_out, Bit_2_3_out, Bit_2_4_out, Bit_2_5_out, Bit_2_6_out, Bit_2_7_out, Bit_2_8_out, Bit_2_out,
       Bit_3_2_out, Bit_3_3_out, Bit_3_4_out, Bit_3_5_out, Bit_3_6_out, Bit_3_7_out, Bit_3_8_out, Bit_3_out;

  not Bit_3 (Bit_3_out, S1);
  not Bit_3_2 (Bit_3_2_out, S0);
  not Bit_3_3 (Bit_3_3_out, S1);
  not Bit_3_4 (Bit_3_4_out, S0);
  not Bit_2 (Bit_2_out, S1);
  not Bit_2_2 (Bit_2_2_out, S0);
  not Bit_2_3 (Bit_2_3_out, S1);
  not Bit_2_4 (Bit_2_4_out, S0);
  not Bit_1 (Bit_1_out, S1);
  not Bit_1_2 (Bit_1_2_out, S0);
  not Bit_1_3 (Bit_1_3_out, S1);
  not Bit_1_4 (Bit_1_4_out, S0);
  not Bit_0 (Bit_0_out, S1);
  not Bit_0_2 (Bit_0_2_out, S0);
  not Bit_0_3 (Bit_0_3_out, S1);
  not Bit_0_4 (Bit_0_4_out, S0);
  and Bit_3_5 (Bit_3_5_out, Bit_3_out, Bit_3_2_out, A3);
  and Bit_3_6 (Bit_3_6_out, Bit_3_3_out, S0, B3);
  and Bit_3_7 (Bit_3_7_out, S1, Bit_3_4_out, C3);
  and Bit_3_8 (Bit_3_8_out, S1, S0, D3);
  and Bit_2_5 (Bit_2_5_out, Bit_2_out, Bit_2_2_out, A2);
  and Bit_2_6 (Bit_2_6_out, Bit_2_3_out, S0, B2);
  and Bit_2_7 (Bit_2_7_out, S1, Bit_2_4_out, C2);
  and Bit_2_8 (Bit_2_8_out, S1, S0, D2);
  and Bit_1_5 (Bit_1_5_out, Bit_1_out, Bit_1_2_out, A1);
  and Bit_1_6 (Bit_1_6_out, Bit_1_3_out, S0, B1);
  and Bit_1_7 (Bit_1_7_out, S1, Bit_1_4_out, C1);
  and Bit_1_8 (Bit_1_8_out, S1, S0, D1);
  and Bit_0_5 (Bit_0_5_out, Bit_0_out, Bit_0_2_out, A0);
  and Bit_0_6 (Bit_0_6_out, Bit_0_3_out, S0, B0);
  and Bit_0_7 (Bit_0_7_out, S1, Bit_0_4_out, C0);
  and Bit_0_8 (Bit_0_8_out, S1, S0, D0);
  or Bit_3_9 (Out3, Bit_3_5_out, Bit_3_6_out, Bit_3_7_out, Bit_3_8_out);
  or Bit_2_9 (Out2, Bit_2_5_out, Bit_2_6_out, Bit_2_7_out, Bit_2_8_out);
  or Bit_1_9 (Out1, Bit_1_5_out, Bit_1_6_out, Bit_1_7_out, Bit_1_8_out);
  or Bit_0_9 (Out0, Bit_0_5_out, Bit_0_6_out, Bit_0_7_out, Bit_0_8_out);
endmodule
