// Logisim project 4.circ as structural Verilog: 1 circuit, main circuit main
module main (
  input  A0,
  input  A1,
  input  A2,
  input  A3,
  input  B0,
  input  B1,
  input  B2,
  input  B3,
  output S0,
  output S1,
  output S2,
  output S3,
  output Cout
);

  wire decoder_1_out1, decoder_1_out2, decoder_1_out3, decoder_1_out4, decoder_1_out5, decoder_1_out6,
       decoder_1_out7, decoder_2_out1, decoder_2_out2, decoder_2_out3, decoder_2_out4, decoder_2_out5,
       decoder_2_out6, decoder_2_out7, decoder_3_out1, decoder_3_out2, decoder_3_out3, decoder_3_out4,
       decoder_3_out5, decoder_3_out6, decoder_3_out7, decoder_4_out1, decoder_4_out2, decoder_4_out3,
       decoder_4_out4, decoder_4_out5, decoder_4_out6, decoder_4_out7;
  wire [2:2] or_2_out, or_3_out, or_5_out;

  Decoder #(.select(3)) decoder_1 (
    .out1(decoder_1_out1), .out2(decoder_1_out2), .out3(decoder_1_out3), .out4(decoder_1_out4),
    .out5(decoder_1_out5), .out6(decoder_1_out6), .out7(decoder_1_out7), .sel({1'b0, A0, B0}));  // open: out0, en
  Decoder #(.select(3)) decoder_2 (
    .out1(decoder_2_out1), .out2(decoder_2_out2), .out3(decoder_2_out3), .out4(decoder_2_out4),
    .out5(decoder_2_out5), .out6(decoder_2_out6), .out7(decoder_2_out7), .sel({or_2_out[2], A1, B1}));  // open: out0, en
  Decoder #(.select(3)) decoder_3 (
    .out1(decoder_3_out1), .out2(decoder_3_out2), .out3(decoder_3_out3), .out4(decoder_3_out4),
    .out5(decoder_3_out5), .out6(decoder_3_out6), .out7(decoder_3_out7), .sel({or_3_out[2], A2, B2}));  // open: out0, en
  Decoder #(.select(3)) decoder_4 (
    .out1(decoder_4_out1), .out2(decoder_4_out2), .out3(decoder_4_out3), .out4(decoder_4_out4),
    .out5(decoder_4_out5), .out6(decoder_4_out6), .out7(decoder_4_out7), .sel({or_5_out[2], A3, B3}));  // open: out0, en
  or or_1 (S0, decoder_1_out1, decoder_1_out2, decoder_1_out4, decoder_1_out7);
  or or_2 (or_2_out[2], decoder_1_out3, decoder_1_out5, decoder_1_out6, decoder_1_out7);
  or or_3 (or_3_out[2], decoder_2_out3, decoder_2_out5, decoder_2_out6, decoder_2_out7);
  or or_4 (S2, decoder_3_out1, decoder_3_out2, decoder_3_out4, decoder_3_out7);
  or or_5 (or_5_out[2], decoder_3_out3, decoder_3_out5, decoder_3_out6, decoder_3_out7);
  or or_6 (S3, decoder_4_out1, decoder_4_out2, decoder_4_out4, decoder_4_out7);
  or or_7 (Cout, decoder_4_out3, decoder_4_out5, decoder_4_out6, decoder_4_out7);
  or or_8 (S1, decoder_2_out1, decoder_2_out2, decoder_2_out4, decoder_2_out7);
endmodule
